// Logisim project 2-bit register(with problem).circ as structural Verilog: 1 circuit, main circuit main
module main (
  input  [1:0] in_1,
  output [1:0] out_2
);

  wire clock_1_out;

  Clock clock_1 (.out(clock_1_out));
  D_flip_flop_main main_1 (.in_1(clock_1_out), .in_2(in_1[1]), .Q(out_2[1]));  // open: nQ
  D_flip_flop_main main_2 (.in_1(clock_1_out), .in_2(in_1[0]), .Q(out_2[0]));  // open: nQ
endmodule
