// Logisim project 2-bit unsigned multiplier.circ as structural Verilog: 1 circuit, main circuit main
module main (
  input  b_1,
  input  b_0,
  input  a_1,
  input  a_0,
  output c_3,
  output c_2,
  output c_1,
  output c_0
);

  wire and_1_out, and_3_out, and_4_out, main_1_out_3;

  and and_1 (and_1_out, b_1, b_1, a_1);
  and and_2 (c_0, b_0, a_0);
  and and_3 (and_3_out, b_1, a_0);
  and and_4 (and_4_out, b_0, a_1);
  _1_bit_half_adder_main main_1 (.in_1(and_3_out), .in_2(and_4_out), .out_3(main_1_out_3), .out_4(c_1));
  _1_bit_half_adder_main main_2 (.in_1(and_1_out), .in_2(main_1_out_3), .out_3(c_3), .out_4(c_2));
endmodule
