// Logisim project D-flip-flop.circ as structural Verilog: 1 circuit, main circuit main
module main (
  input  in_1,
  input  in_2,
  output Q,
  output nQ
);

  wire main_1_out_3, not_1_out;

  not not_1 (not_1_out, in_1);
  D_Latch_main main_1 (.in_1(in_1), .in_2(in_2), .out_3(main_1_out_3));  // open: out_4
  D_Latch_main main_2 (.in_1(not_1_out), .in_2(main_1_out_3), .out_3(Q), .out_4(nQ));
endmodule
